# Fritzing sketch OpenFFBYoke (saved by Fritzing 0.9.4)

parts:
  Composant1 = Arduino Leonardo (Rev3b)
  S1 = Pushbutton [package="[THT]"]
  S2 = Pushbutton [package="[THT]"]

nets:
  N1: Composant1.D4/A6, S1.Pin_4
  N2: Composant1.D5_PWM, S2.Pin_4

notes:
  Encoder 1 A
  Encoder 1 B
  Encoder 2 A
  Encoder 2 B
  BP2
  BP1
  Dir motor Y
  Reverse dir motor Y
  PWM motor X -> pin 3,4
  PWM motor Y
  Reverse dir motor X -> pin 2
  Dir motor X-> pin1
  BTS7960B
